// Digital circuit MUX.dig as structural Verilog
module MUX (
  input  D,
  input  C,
  input  B,
  input  A,
  output Y
);

  wire notconnected_1_out, notconnected_2_out, notconnected_3_out, notconnected_4_out;

  // NotConnected on notconnected_1_out
  // NotConnected on notconnected_2_out
  // NotConnected on notconnected_3_out
  // NotConnected on notconnected_4_out
  Multiplexer #(.Selector_Bits(3)) multiplexer_1 (
    .sel({1'b0, A, D}), .in_0(1'b0), .in_1(1'b1), .in_2(1'b1), .in_3(1'b0), .in_4(notconnected_1_out),
    .in_5(notconnected_2_out), .in_6(notconnected_3_out), .in_7(notconnected_4_out), .out(Y));

  // Notes on the sheet:
  //   Use A as the most-significant bit and 
  //   D as the least-significant bit.
  //   Converts between single bits & a 3-bit bus
endmodule

/* Test case:
A B C D Y
0 0 0 0 X
0 0 0 1 1
*/
